// Logisim project Carry Lookahead Adder.circ as structural Verilog: 3 circuits, main circuit CLA Generator
// CLA Logic
module CLA_Generator (
  input  c0,
  input  g0,
  input  g1,
  input  g2,
  input  g3,
  input  p0,
  input  p1,
  input  p2,
  input  p3,
  output C1,
  output C2,
  output C3,
  output C4
);

  wire and_1_out, and_2_out, and_3_out, and_4_out, and_5_out, and_6_out, and_7_out, and_8_out, and_9_out,
       and_10_out;

  and and_1 (and_1_out, c0, p3, p2, p1, p0);
  and and_2 (and_2_out, g3, p2, p1, p0);
  and and_3 (and_3_out, g2, p1, p0);
  and and_4 (and_4_out, g1, p0);
  and and_5 (and_5_out, c0, p3, p2, p1);
  and and_6 (and_6_out, g3, p2, p1);
  and and_7 (and_7_out, g2, p1);
  and and_8 (and_8_out, c0, p2, p3);
  and and_9 (and_9_out, p2, g3);
  and and_10 (and_10_out, c0, p3);
  or or_1 (C1, and_1_out, and_2_out, and_3_out, and_4_out, g0);
  or or_2 (C2, and_5_out, and_6_out, and_7_out, g1);
  or or_3 (C3, and_8_out, and_9_out, g2);
  or or_4 (C4, and_10_out, g3);

  // Notes on the sheet:
  //   Carry Lookahead Logic
endmodule

// 1-bit FA
module Full_Adder (
  input  A,
  input  B,
  input  C,
  output Generate,
  output Propagate,
  output Sum
);

  wire xor_1_out;

  xor xor_1 (xor_1_out, A, B);
  and and_1 (Generate, A, B);
  or or_1 (Propagate, A, B);
  xor xor_2 (Sum, xor_1_out, C);

  // Notes on the sheet:
  //   Full Adder
endmodule

module CLA (
  input  A3,
  input  B3,
  input  A2,
  input  B2,
  input  A1,
  input  B1,
  input  A0,
  input  B0,
  input  Cin,
  output Cout,
  output S3,
  output S2,
  output S1,
  output S0
);

  wire cla_generator_1_c1, cla_generator_1_c2, cla_generator_1_c3, full_adder_1_generate,
       full_adder_1_propagate, full_adder_2_generate, full_adder_2_propagate, full_adder_3_generate,
       full_adder_3_propagate, full_adder_4_generate, full_adder_4_propagate;

  Full_Adder full_adder_1 (
    .A(A3), .B(B3), .C(cla_generator_1_c3), .Sum(S3), .Propagate(full_adder_1_propagate),
    .Generate(full_adder_1_generate));
  CLA_Generator cla_generator_1 (
    .c0(Cin), .C2(cla_generator_1_c2), .C4(Cout), .C3(cla_generator_1_c3), .C1(cla_generator_1_c1),
    .g0(full_adder_4_generate), .g1(full_adder_3_generate), .p1(full_adder_3_propagate),
    .g2(full_adder_2_generate), .g3(full_adder_1_generate), .p0(full_adder_4_propagate),
    .p2(full_adder_2_propagate), .p3(full_adder_1_propagate));
  Full_Adder full_adder_2 (
    .A(A2), .B(B2), .C(cla_generator_1_c2), .Sum(S2), .Propagate(full_adder_2_propagate),
    .Generate(full_adder_2_generate));
  Full_Adder full_adder_3 (
    .A(A1), .B(B1), .C(cla_generator_1_c1), .Sum(S1), .Propagate(full_adder_3_propagate),
    .Generate(full_adder_3_generate));
  Full_Adder full_adder_4 (
    .A(A0), .B(B0), .C(Cin), .Sum(S0), .Propagate(full_adder_4_propagate), .Generate(full_adder_4_generate));

  // Notes on the sheet:
  //   Carry Lookahead Adder
endmodule
